// Logisim project Proj2starter.circ as structural Verilog: 4 circuits, main circuit regfile
module CPUmain (
  input  [31:0] in_1
);

  wire control_1_imm_sel, control_1_reg_write_e;
  wire [3:0] control_1_alu_code;
  wire [4:0] control_1_rd, control_1_rs, control_1_rt;
  wire [31:0] alu_1_res, control_1_imm, multiplexer_1_out, regfile_1_rs_data, regfile_1_rt_data;

  regfile regfile_1 (
    .rt(control_1_rt), .rd(control_1_rd), .rd_data(alu_1_res), .write_e(control_1_reg_write_e),
    .rs(control_1_rs), .rs_data(regfile_1_rs_data), .rt_data(regfile_1_rt_data));
  Control control_1 (
    .Inst(in_1), .rs(control_1_rs), .rt(control_1_rt), .rd(control_1_rd), .imm(control_1_imm),
    .reg_write_e(control_1_reg_write_e), .imm_sel(control_1_imm_sel), .ALU_code(control_1_alu_code));
  Multiplexer #(.width(32)) multiplexer_1 (
    .in0(regfile_1_rt_data), .in1(control_1_imm), .out(multiplexer_1_out), .sel(control_1_imm_sel));
  Bit_Extender bit_extender_1 ();  // open: in, out
  ALU alu_1 (.OP2(multiplexer_1_out), .OP1(regfile_1_rs_data), .ALU_CODE(control_1_alu_code), .Res(alu_1_res));

  // Notes on the sheet:
  //   SHOULD AT LEAST WORK FOR ADD, ADDI AND MULT
  //   SET THIS TO 0 IF YOU DO NOT WANT TO OVERWRITE REGISTERS ... EX MULT -- HI AND LOW LIVE  IN THE ALU
  //   FOR MULT YOU DON'T WANT TO CHANGE ANY REGISTERS
  //   MULITPLEXER USED TO DETERMINE WHETHER IT IS I TYPE OR R TYPE
  //   BASICALLLY MAKE THIS = TO ZERO TO TAKE THE R TYPE 
  //   USE THIS TO EXTEND NON 32 BIT NUMBERS INTO SIGNED 32 BIT NUMBERS
  //   ALU DOES ALL OPERATIONS ON EVERY OP1 AND OP2 FROM THE REGISTERS -- HOWEVER YOU NEED TO SPECIFY WHICH ONE TO GET FROM THE ALU CODE
endmodule

module regfile (
  input  [4:0] rs,
  input  [4:0] rt,
  input  [4:0] rd,
  input  write_e,
  input  [31:0] rd_data,
  output [31:0] rs_data,
  output [31:0] rt_data
);

  Register Reg1_at ();  // open: D, en, clk, Q, clr
endmodule

module ALU (
  input  [31:0] OP1,
  input  [31:0] OP2,
  input  [3:0] ALU_CODE,
  output [31:0] Res
);

  wire comparator_1_gt, comparator_2_eq, comparator_3_eq, or_1_out;
  wire [31:0] adder_1_out, bit_extender_1_out, divider_1_out, HI_q, LO_q, multiplier_1_out, shifter_1_out,
       shifter_2_out, subtractor_1_out;

  Adder #(.width(32)) adder_1 (.a(OP1), .b(OP2), .out(adder_1_out));  // open: cin, cout
  Subtractor #(.width(32)) subtractor_1 (.a(OP1), .b(OP2), .out(subtractor_1_out));  // open: bin, bout
  Multiplier #(.width(32)) multiplier_1 (.a(OP1), .b(OP2), .out(multiplier_1_out));  // open: cin, cout
  Divider #(.width(32)) divider_1 (.a(OP1), .b(OP2), .out(divider_1_out));  // open: upper, rem
  Shifter #(.width(32)) shifter_1 (.in(OP1), .\dist (OP2[4:0]), .out(shifter_1_out));
  Shifter #(.shift("lr"), .width(32)) shifter_2 (.in(OP1), .\dist (OP2[4:0]), .out(shifter_2_out));
  Comparator #(.width(32)) comparator_1 (.a(OP1), .b(OP2), .gt(comparator_1_gt));  // open: eq, lt
  assign bit_extender_1_out = {{31{comparator_1_gt}}, comparator_1_gt};  // Bit_Extender bit_extender_1
  Multiplexer #(.select(4), .width(32)) multiplexer_1 (
    .in0(adder_1_out), .in1(subtractor_1_out), .in2(multiplier_1_out), .in3(divider_1_out), .in4(HI_q),
    .in5(LO_q), .in6(shifter_1_out), .in7(shifter_2_out), .in8(bit_extender_1_out), .in9({32{1'b0}}),
    .in10({32{1'b0}}), .in11({32{1'b0}}), .in12({32{1'b0}}), .in13({32{1'b0}}), .in14({32{1'b0}}),
    .in15({32{1'b0}}), .out(Res), .sel(ALU_CODE));
  Comparator #(.width(4)) comparator_2 (.a(4'b1000), .b(ALU_CODE), .eq(comparator_2_eq));  // open: gt, lt
  Comparator #(.width(4)) comparator_3 (.a(4'b1001), .b(ALU_CODE), .eq(comparator_3_eq));  // open: gt, lt
  or or_1 (or_1_out, comparator_2_eq, comparator_3_eq);
  Register #(.width(32)) HI (.en(or_1_out), .Q(HI_q));  // open: D, clk, clr
  Register #(.width(32)) LO (.en(or_1_out), .Q(LO_q));  // open: D, clk, clr

  // Notes on the sheet:
  //   I HAVE UPDATED THIS A LOT.... REVERT TO OTHER ONE FOR THE SETUP JUST FROM CLASS
  //   these are shifts will have to check them
  //   breaking it into 5 bits and 27 bits cause it doesnt seem to work past 5 with the shifter? figure out how this works better
  //   thinking about what we have to do.... if the ALU code is anything but mult or divide we take the outputs and output them... if it is div or mult we dont output anything but instead store values into HI or LO
  //   pretty sure this works cause div and mult are made to not change the Res in the main?
  //   THIS IS NOT DONE I HAVE NO IDEA HOW TO GET THE REMAINDER
endmodule

module Control (
  input  [31:0] Inst,
  output [4:0] rs,
  output [4:0] rt,
  output [4:0] rd,
  output [31:0] imm,
  output reg_write_e,
  output imm_sel,
  output [3:0] ALU_code
);

  Bit_Extender bit_extender_1 ();  // open: in, out

  // Notes on the sheet:
  //   USE THIS TO RETURN ONLY 32 BIT NUMBERS AND TO EXTEND IT
endmodule
